# Fritzing sketch garage (saved by Fritzing 0.9.3b)
breadboards: 1

parts:
  U1 = ESP32S-HiLetgo [part_number=ESP32S-HiLetgo]
  LED2 = LED - 5mm [color="Red (633nm)" package="5 mm [THT]"]
  LED3 = LED - 5mm [color="Red (633nm)" package="5 mm [THT]"]
  LED4 = LED - 5mm [color="Red (633nm)" package="5 mm [THT]"]
  LED5 = LED - 5mm [color="Red (633nm)" package="5 mm [THT]"]
  LED6 = LED - 5mm [color="Red (633nm)" package="5 mm [THT]"]
  LED7 = LED - 5mm [color="Red (633nm)" package="5 mm [THT]"]
  Part1 = KY-009 Full Color RGB LED SMD Module [package="Breakout board"]
  J1 = Basic Servo
  LED8 = LED - 5mm [color="Yellow (585nm)" package="5 mm [THT]"]
  LED9 = LED - 5mm [color="Yellow (585nm)" package="5 mm [THT]"]
  LED10 = LED - 5mm [color="Yellow (585nm)" package="5 mm [THT]"]
  R1 = Resistor [tolerance=±5% resistance=220 package=THT]
  R3 = Resistor [tolerance=±5% resistance=220 package=THT]
  R4 = Resistor [tolerance=±5% resistance=220 package=THT]
  R5 = Resistor [tolerance=±5% resistance=220 package=THT]
  Composant1 = SRF05 Ultrasonic Rangefinder
  Water_Level_Sensor1 = Water Level Sensor

nets:
  N1: U1.GPIO33, Water_Level_Sensor1.SIG
  N2: U1.GPIO25, R5.Pin_0
  N3: U1.GPIO26, R1.Pin_1
  N4: U1.GPIO14, R3.Pin_1
  N5: U1.GPIO12, R4.Pin_1
  GND: U1.GND, LED2.cathode, LED3.cathode, LED5.cathode, LED6.cathode, LED7.cathode, Part1.-, J1.gnd, LED8.cathode, LED9.cathode, LED10.cathode, Composant1.GND, Water_Level_Sensor1.GND
  VCC: U1.VIN, LED4.cathode, J1.vcc, Composant1.VCC, Water_Level_Sensor1.VCC
  N6: U1.GPIO2, Part1.R
  N7: U1.GPIO4, Part1.G
  N8: U1.GPIO16, Part1.B
  N9: U1.GPIO5, Composant1.Echo
  N10: U1.GPIO18, Composant1.Trig
  N11: U1.GPIO19, J1.pulse
  N12: LED2.anode, LED6.anode, R5.Pin_1
  N13: LED3.anode, LED4.anode, R3.Pin_0
  N14: LED5.anode, LED7.anode, R1.Pin_0
  N15: LED8.anode, LED9.anode, LED10.anode, R4.Pin_0

custom parts:
  ESP32S-HiLetgo: HiLetgo ESP-WROOM-32 ESP32 ESP-32S Development Board 2.4GHz Dual-Mode WiFi + Bluetooth Dual Cores Microcontroller The ESP32 integrated with Antenna switches, RF Balun, power amplifiers, low-noise amplifiers, filters, and management modules, and the entire solution occupies the least area of PCB. 2.4 GHz Wi-Fi plus Bluetooth dual-mode chip, with TSMC Ultra-low power consumption 40nm technology,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
  KY-009 Full Color RGB LED SMD Module: RGB full color LED Module KY-009 for Arduino, emits a range of colors by mixing red, green and blue. The amount of each primary color is adjusted using PWM.
  Water Level Sensor: A water level sensor. This sensor operates at 3V to 5V. The Sig (signal) pin outputs an analogue signal that is in proportion to the amount of water in contact with the sensor.
