# Fritzing sketch hall (saved by Fritzing 0.9.3b)
breadboards: 1

parts:
  U1 = ESP32S-HiLetgo [part_number=ESP32S-HiLetgo]
  Part1 = KY-010 Photo Interrupter Module [package="Breakout board"]
  J1 = Basic Servo
  Keyes1 = Keyes IR Infrared Sensor Switch Module
  Keyes2 = Keyes IR Infrared Sensor Switch Module

nets:
  N1: U1.GPIO25, J1.pulse
  GND: U1.GND, Part1.-, J1.gnd, Keyes1.GND, Keyes2.GND
  VCC: U1.VIN, Part1.Vin, J1.vcc, Keyes1.VCC, Keyes2.VCC
  N2: U1.GPIO18, Part1.S
  N3: U1.GPIO22, Keyes1.out
  N4: U1.GPIO23, Keyes2.out

custom parts:
  ESP32S-HiLetgo: HiLetgo ESP-WROOM-32 ESP32 ESP-32S Development Board 2.4GHz Dual-Mode WiFi + Bluetooth Dual Cores Microcontroller The ESP32 integrated with Antenna switches, RF Balun, power amplifiers, low-noise amplifiers, filters, and management modules, and the entire solution occupies the least area of PCB. 2.4 GHz Wi-Fi plus Bluetooth dual-mode chip, with TSMC Ultra-low power consumption 40nm technology,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
  KY-010 Photo Interrupter Module: Photo Interrupter Module Keyes KY-010 for Arduino, will trigger a signal when light between the sensor's gap is blocked.
  Keyes IR Infrared Sensor Switch Module: An infrared obstacle detector
