# Fritzing sketch salon (saved by Fritzing 0.9.3b)
breadboards: 1

parts:
  U1 = ESP32S-HiLetgo [part_number=ESP32S-HiLetgo]
  R1 = Resistor [tolerance=±5% resistance=220 package=THT]
  Part1 = KY-018 Photoresistor Module [package="Breakout board"]
  LED1 = LED - 5mm [color="Red (633nm)" package="5 mm [THT]"]
  LED2 = LED - 5mm [color="Red (633nm)" package="5 mm [THT]"]
  LED3 = LED - 5mm [color="Red (633nm)" package="5 mm [THT]"]
  J1 = Basic Servo
  J3 = Basic Servo

nets:
  N1: U1.GPIO32, R1.Pin_1
  N2: U1.GPIO33, Part1.S
  N3: U1.GPIO12, J3.pulse
  GND: U1.GND, Part1.-, LED1.cathode, LED2.cathode, LED3.cathode, J1.gnd, J3.gnd
  VIN: U1.VIN, Part1.Vin, J1.vcc, J3.vcc
  N4: U1.GPIO22, J1.pulse
  N5: R1.Pin_0, LED1.anode, LED2.anode, LED3.anode

custom parts:
  ESP32S-HiLetgo: HiLetgo ESP-WROOM-32 ESP32 ESP-32S Development Board 2.4GHz Dual-Mode WiFi + Bluetooth Dual Cores Microcontroller The ESP32 integrated with Antenna switches, RF Balun, power amplifiers, low-noise amplifiers, filters, and management modules, and the entire solution occupies the least area of PCB. 2.4 GHz Wi-Fi plus Bluetooth dual-mode chip, with TSMC Ultra-low power consumption 40nm technology,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
  KY-018 Photoresistor Module: KY-018 Photoresistor module, used to measure light intensity. It can determine the presence or absence of light.
