# Fritzing sketch sdb (saved by Fritzing 0.9.3b)
breadboards: 1

parts:
  U1 = ESP32S-HiLetgo [part_number=ESP32S-HiLetgo]
  R1 = Resistor [tolerance=±5% resistance=220 package=THT]
  Part1 = KY-012 Active Buzzer Module [package="Breakout board"]
  DHT1 = DHT11 Humitidy and Temperature Sensor
  Part2 = KY-008 Laser Transmitter Module [package="Breakout board"]
  J1 = Generic male header - 3 pins [form="♂ (male)" package=THT]
  LED1 = LED - 5mm [color="Red (633nm)" package="5 mm [THT]"]
  LED2 = LED - 5mm [color="Red (633nm)" package="5 mm [THT]"]
  LED3 = LED - 5mm [color="Red (633nm)" package="5 mm [THT]"]

nets:
  N1: U1.GPIO32, DHT1.VDD
  N2: U1.GPIO25, R1.Pin_1
  GND: U1.GND, Part1.-, DHT1.GND, Part2.-, J1.pin2
  N3: U1.VIN, DHT1.NULL, J1.pin1, LED1.anode, LED2.anode, LED3.anode
  N4: U1.GPIO16, Part1.S
  N5: U1.GPIO18, Part2.S, J1.pin3
  N6: R1.Pin_0, LED1.cathode, LED2.cathode, LED3.cathode

custom parts:
  ESP32S-HiLetgo: HiLetgo ESP-WROOM-32 ESP32 ESP-32S Development Board 2.4GHz Dual-Mode WiFi + Bluetooth Dual Cores Microcontroller The ESP32 integrated with Antenna switches, RF Balun, power amplifiers, low-noise amplifiers, filters, and management modules, and the entire solution occupies the least area of PCB. 2.4 GHz Wi-Fi plus Bluetooth dual-mode chip, with TSMC Ultra-low power consumption 40nm technology,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
  KY-012 Active Buzzer Module: Active Piezoelectric Buzzer Module Keyes KY-012, it produces single-tone sound when signal is high.
  DHT11 Humitidy and Temperature Sensor: DHT11 Humidity and Temperature Sensor
  KY-008 Laser Transmitter Module: Laser Transmitter module KY-008 for Arduino, emits a dot shaped red laser beam.
  Generic male header - 3 pins: Generic male header
